# Fritzing sketch CharliePlexedLampFieldv2a (saved by Fritzing 0.9.3b)
circuit board: 15.3755cm x 3.52889cm
breadboards: 1

parts:
  R1 = Resistor [tolerance=±5% resistance=220 package=THT]
  R2 = Resistor [tolerance=±5% resistance=220 package=THT]
  R3 = Resistor [tolerance=±5% resistance=220 package=THT]
  R4 = Resistor [tolerance=±5% resistance=220 package=THT]
  R5 = Resistor [tolerance=±5% resistance=220 package=THT]
  R6 = Resistor [tolerance=±5% resistance=220 package=THT]
  LED1 = LED - 3mm [color="Red (633nm)" package="3 mm [THT]"]
  LED2 = LED - 3mm [color="Red (633nm)" package="3 mm [THT]"]
  LED3 = LED - 3mm [color="Red (633nm)" package="3 mm [THT]"]
  LED4 = LED - 3mm [color="Red (633nm)" package="3 mm [THT]"]
  LED5 = LED - 3mm [color="Red (633nm)" package="3 mm [THT]"]
  LED6 = LED - 3mm [color="Red (633nm)" package="3 mm [THT]"]
  LED7 = LED - 3mm [color="Red (633nm)" package="3 mm [THT]"]
  LED8 = LED - 3mm [color="Red (633nm)" package="3 mm [THT]"]
  LED9 = LED - 3mm [color="Red (633nm)" package="3 mm [THT]"]
  LED10 = LED - 3mm [color="Red (633nm)" package="3 mm [THT]"]
  LED11 = LED - 3mm [color="Red (633nm)" package="3 mm [THT]"]
  LED12 = LED - 3mm [color="Red (633nm)" package="3 mm [THT]"]
  LED13 = LED - 3mm [color="Red (633nm)" package="3 mm [THT]"]
  LED14 = LED - 3mm [color="Red (633nm)" package="3 mm [THT]"]
  LED15 = LED - 3mm [color="Red (633nm)" package="3 mm [THT]"]
  LED16 = LED - 3mm [color="Red (633nm)" package="3 mm [THT]"]
  LED17 = LED - 3mm [color="Red (633nm)" package="3 mm [THT]"]
  LED18 = LED - 3mm [color="Red (633nm)" package="3 mm [THT]"]
  LED19 = LED - 3mm [color="Red (633nm)" package="3 mm [THT]"]
  LED20 = LED - 3mm [color="Red (633nm)" package="3 mm [THT]"]
  LED21 = LED - 3mm [color="Red (633nm)" package="3 mm [THT]"]
  LED22 = LED - 3mm [color="Red (633nm)" package="3 mm [THT]"]
  LED23 = LED - 3mm [color="Red (633nm)" package="3 mm [THT]"]
  LED24 = LED - 3mm [color="Red (633nm)" package="3 mm [THT]"]
  LED25 = LED - 3mm [color="Red (633nm)" package="3 mm [THT]"]
  LED26 = LED - 3mm [color="Red (633nm)" package="3 mm [THT]"]
  JP2 = Header 6 [package=molex-1x6-ra_lock]

nets:
  N1: R1.Pin_0, JP2.1
  N2: R1.Pin_1, LED1.anode, LED2.cathode, LED3.anode, LED4.cathode, LED7.anode, LED8.cathode, LED13.anode, LED14.cathode, LED21.anode, LED22.cathode
  N3: R2.Pin_0, JP2.2
  N4: R2.Pin_1, LED1.cathode, LED2.anode, LED5.anode, LED6.cathode, LED9.anode, LED10.cathode, LED15.anode, LED16.cathode, LED23.anode, LED24.cathode
  N5: R3.Pin_0, JP2.3
  N6: R3.Pin_1, LED3.cathode, LED4.anode, LED5.cathode, LED6.anode, LED11.anode, LED12.cathode, LED17.anode, LED18.cathode, LED25.anode, LED26.cathode
  N7: R4.Pin_0, JP2.4
  N8: R4.Pin_1, LED7.cathode, LED8.anode, LED9.cathode, LED10.anode, LED11.cathode, LED12.anode, LED19.anode, LED20.cathode
  N9: R5.Pin_0, JP2.6
  N10: R5.Pin_1, LED13.cathode, LED14.anode, LED15.cathode, LED16.anode, LED17.cathode, LED18.anode, LED19.cathode, LED20.anode
  N11: R6.Pin_0, JP2.5
  N12: R6.Pin_1, LED21.cathode, LED22.anode, LED23.cathode, LED24.anode, LED25.cathode, LED26.anode

notes:
  Q
  W
  E
  R
  T
  Z
  U
  I
  O
  A
  S
  D
  F
  G
  H
  J
  K
  P
  Y
  X
  C
  V
  B
  N
  M
  L
  external lampfield v1   2017    http://arduinoenigma.blogspot.com
